# Fritzing sketch Esp8266 (saved by Fritzing 0.8.7b)
breadboards: 1

parts:
  U1 = NodeMCU V1.0
  Mod1 = OLED Mono 0.56 inch blue or white
  DHT1 = DHT11 Humitidy and Temperature Sensor
  R1 = Temperature Sensor (Thermistor) [thermistor_type=NTC package=THT]
  R2 = Resistor [tolerance=±5% resistance=220 package=THT]
  CO2 = Adafruit CCS811 [part_number="Adafruit #3566"]
  LED1 = LED - 5mm [color="Red (633nm)" package="5 mm [THT]"]
  R3 = Resistor [tolerance=±5% resistance=220 package=THT]
  R4 = Resistor [tolerance=±5% resistance=220 package=THT]
  LED2 = LED - 5mm [color="Red (633nm)" package="5 mm [THT]"]
  U2 = Voltage Regulator - 5V [package="TO220 [THT]"]
  C2 = Ceramic Capacitor [capacitance=0pF package="100 mil [THT, multilayer]"]
  C3 = Ceramic Capacitor [capacitance=100nF package="100 mil [THT, multilayer]"]
  R5 = Resistor [tolerance=±5% resistance=220 package=THT]
  R6 = Resistor [tolerance=±5% resistance=220 package=THT]
  S2 = Pushbutton [package=THT]
  R7 = Resistor [tolerance=±5% resistance=220 package=THT]

nets:
  N1: U1.D0, U1.RST
  N2: U1.D1, Mod1.SCL, CO2.SCL
  N3: U1.D2, Mod1.SDA, CO2.SDA
  N4: U1.D3, DHT1.DATA
  GND: U1.GND, Mod1.GND, DHT1.GND, R1.pin_0, CO2.GND, CO2.!WAKE, LED1.cathode, LED2.cathode, U2.GND, C2.0, C3.0, R6.Pin_1, R7.Pin_1
  N5: U1.D6, R3.Pin_0
  N6: U1.D7, R4.Pin_0
  N7: U1.D8, S2.leg0, R7.Pin_0
  5V: U1.Vin, Mod1.VCC, U2.output_voltage, C2.1, R5.Pin_0
  N8: U1.A0, R1.pin_1, R2.Pin_1
  3.3V: DHT1.VDD, R2.Pin_0, CO2.3.3V, R5.Pin_1, R6.Pin_0, S2.leg1
  N9: LED1.anode, R3.Pin_1
  N10: R4.Pin_1, LED2.anode
  12V: U2.input_voltage, C3.1

custom parts:
  NodeMCU V1.0: ESP8266 based NodeMCU
  OLED Mono 0.56 inch blue or white: OLED, I2C 3.3V - 5V Blue and White text versions
  DHT11 Humitidy and Temperature Sensor: DHT11 Humidity and Temperature Sensor
  Adafruit CCS811: Breathe easy - we finally have an I2C VOC/eCO2 sensor in the Adafruit shop! Add air quality monitoring to your project and with an Adafruit CCS811 Air Quality Sensor Breakout. This sensor from AMS is a gas sensor that can detect a wide range of Volatile Organic Compounds (VOCs) and is intended for indoor air quality monitoring. When connected to your microcontroller (running our library code)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
